# Fritzing sketch LDR (saved by Fritzing 0.9.2b)
breadboards: 1

parts:
  Parte1 = Arduino Nano (Rev3.0)
  J1 = Piezo Speaker
  R1 = Resistor [tolerance=±5% resistance=220 package=THT]
  R2 = Photocell (LDR) [package=THT]

nets:
  N1: Parte1.D12/MISO, J1.pin2
  N2: Parte1.GND, J1.pin1, R2.pin_1
  N3: Parte1.5V, R1.Pin_0
  N4: Parte1.A0, R1.Pin_1, R2.pin_0
