# Fritzing sketch Led PWM (saved by Fritzing 0.9.0b)
breadboards: 1

parts:
  Parte1 = Arduino Nano (Rev3.0)
  R1 = Resistor [tolerance=±5% resistance=330 package=THT]
  LED1 = LED - 5mm [color="Red (633nm)" package="5 mm [THT]"]

nets:
  N1: Parte1.GND, LED1.cathode
  N2: Parte1.D9, R1.Pin_1
  N3: R1.Pin_0, LED1.anode
