# Fritzing sketch Potenciometro (saved by Fritzing 0.9.0b)
breadboards: 1

parts:
  Parte1 = Arduino Nano (Rev3.0)
  U1 = POT [package=pot_alpha_rv16af-20]

nets:
  N1: Parte1.GND, U1.A
  N2: Parte1.5V, U1.E
  N3: Parte1.A5, U1.S
