# Fritzing sketch dht11 (saved by Fritzing 0.9.2b)
breadboards: 1

parts:
  Parte1 = Arduino Nano (Rev3.0)
  RHT1 = Humidity and Temperature Sensor RHT03
  R1 = Resistor [tolerance=±5% resistance=220 package=THT]

nets:
  N1: Parte1.D2, RHT1.Data-signal, R1.Pin_0
  N2: Parte1.GND, RHT1.GND_2
  5V: Parte1.5V, RHT1.Vcc, R1.Pin_1
