# Fritzing sketch motorcc (saved by Fritzing 0.9.0b)
breadboards: 1

parts:
  Parte1 = Arduino Nano (Rev3.0)
  Q1 = NPN-Transistor [package="TO92 [THT]"]
  LED1 = LED - 5mm [color="Red (633nm)" package="5 mm [THT]"]
  M1 = DC Motor
  R1 = Resistor [tolerance=±5% resistance=330 package=THT]  # not connected

nets:
  N1: Parte1.GND, LED1.cathode, M1.pin_2
  N2: Parte1.5V, Q1.C
  N3: Q1.E, LED1.anode, M1.pin_1
