# Fritzing sketch tilt (saved by Fritzing 0.9.2b)
breadboards: 1

parts:
  Parte1 = Arduino Nano (Rev3.0)
  S1 = Tilt Switch [package=THT]
  R1 = Resistor [tolerance=±5% resistance=220 package=THT]
  LED1 = LED - 5mm [color="Red (633nm)" package="5 mm [THT]"]

nets:
  N1: Parte1.GND, S1.Pin_2, LED1.cathode
  N2: Parte1.D2, S1.Pin_1, R1.Pin_1
  N3: Parte1.5V, R1.Pin_0
  N4: Parte1.D13/SCK, LED1.anode
